# Fritzing sketch Plantthing (saved by Fritzing 0.9.2b)
breadboards: 1

parts:
  Part1 = Arduino Uno (Rev3)
  LED1 = RGB LED (com. cathode, rgb) [package="5 mm [THT]"]
  R1 = Resistor [tolerance=±5% resistance=330 package=THT]
  R2 = Resistor [tolerance=±5% resistance=330 package=THT]
  R3 = Resistor [tolerance=±5% resistance=330 package=THT]
  R4 = Photocell (LDR) [package=THT]
  R5 = Resistor [tolerance=±5% resistance=10k package=THT]
  R6 = Resistor [tolerance=±5% resistance=330 package=THT]
  LED2 = LED - 5mm [color="Red (633nm)" package="5 mm [THT]"]
  LED3 = LED - 5mm [color="Yellow (592nm)" package="5 mm [THT]"]
  LED4 = LED - 5mm [color="Green (555nm)" package="5 mm [THT]"]
  R7 = Resistor [tolerance=±5% resistance=330 package=THT]
  R8 = Resistor [tolerance=±5% resistance=330 package=THT]

nets:
  N1: Part1.A2, R4.pin_1, R5.Pin_1
  N2: Part1.D9_PWM, R1.Pin_1
  N3: Part1.D10_PWM/SS, R2.Pin_1
  N4: Part1.D11_PWM/MOSI, R3.Pin_1
  N5: Part1.D3_PWM, LED4.cathode
  N6: Part1.D5_PWM, LED3.cathode
  N7: Part1.D7, LED2.cathode
  N8: Part1.5V, R5.Pin_0
  N9: Part1.GND, R4.pin_0, R6.Pin_0, R7.Pin_0, R8.Pin_0
  N10: LED1.red_anode, R3.Pin_0
  N11: LED1.common_cathode, R2.Pin_0
  N12: LED1.blue_anode, R1.Pin_0
  N13: R6.Pin_1, LED2.anode
  N14: LED3.anode, R7.Pin_1
  N15: LED4.anode, R8.Pin_1

notes:
  Rain/Moisture sensor:
  http://www.dx.com/p/raindrops-sensor-module-blue-black-199859#.VkudON-rRE6
